# Fritzing sketch architecture (saved by Fritzing 1.0.5)

parts:
  U1 = LuaNode32 / ESP32 [part_number=ESP32S-PIN30]
  Capacitive_Soil_Moisture_Sensor1 = DFRobot Capacitive Soil Moisture Sensor V1.0 [part_number=SEN0193]
  A1 = 2 channel relay module [package=THT]
  JACK1 = 2.1mm Barrel Jack with Terminal Block
  Mini_Water_Pump_3-6VDC1 = Mini Water Pump 3-6VDC [part_number="Mini Water Pump 3-6VDC" chip_label=IC package="DIP (Dual Inline) [THT]"]

nets:
  N1: U1.VN, A1.pin_13
  N2: U1.D34, Capacitive_Soil_Moisture_Sensor1.A
  GND: U1.GND, Capacitive_Soil_Moisture_Sensor1.GND, A1.pin_14
  3V3: U1.3V3, Capacitive_Soil_Moisture_Sensor1.VCC
  N3: U1.D23, A1.pin_15
  N4: A1.pin_4, Mini_Water_Pump_3-6VDC1.+M
  N5: A1.pin_5, JACK1.POS
  N6: JACK1.NEG, Mini_Water_Pump_3-6VDC1.-M

custom parts:
  LuaNode32 / ESP32: New Image for LuaNode32 DOIT ESP32 DEVKIT V1. Base parts from LuaNode32 / ESP32 ESP32 based LuaNode32 by G.Noorlander DOIT Esp32 DevKit v1 (30 pins long, 11 pins width) by Werner Rothschopf (modified by vanepp Dec 2018)
  DFRobot Capacitive Soil Moisture Sensor V1.0: DFRobot Capacitive Soil Moisture Sensor V1.0 This product measures soil moisture levels by capacitive sensing, rather than resistive sensing like other types of moisture sensor. It is made of a corrosion resistant material giving it a long service life. Insert it into soil and impress your friends with the real-time soil moisture data! The product includes an on-board voltage regulator which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
  2 channel relay module: 2 channel Relay Module 5V 12V 24V High and Low Level Trigger Relay Control With Optocoupler Two Way relays DC 5 V 12 V 24 V Volt.
